# Fritzing sketch traffic-lights (saved by Fritzing 0.9.3b)
circuit board: 11.135cm x 5.72246cm
breadboards: 1

parts:
  Componente1 = Arduino Mega 2560 (Rev3)
  R1 = Resistor [tolerance=±5% resistance=220 package=THT]
  R2 = Resistor [tolerance=±5% resistance=220 package=THT]
  R3 = Resistor [tolerance=±5% resistance=220 package=THT]
  LED1 = LED - 5mm [color="Red (633nm)" package="5 mm [THT]"]
  LED2 = LED - 5mm [color="Yellow (595nm)" package="5 mm [THT]"]
  LED3 = LED - 5mm [color="Green (555nm)" package="5 mm [THT]"]

nets (from the schematic view):
  N1: Componente1.GND, LED1.anode, LED2.anode, LED3.anode
  N2: Componente1.D4_PWM, R3.Pin_1
  N3: Componente1.D5_PWM, R2.Pin_1
  N4: Componente1.D6_PWM, R1.Pin_0
  N5: R1.Pin_1, LED1.cathode
  N6: R2.Pin_0, LED2.cathode
  N7: R3.Pin_0, LED3.cathode
